// Logisim project TinyCPU.circ as structural Verilog: 14 circuits, main circuit TinyCPU
module AddSub (
  input  [31:0] OPERANDS,
  input  SUBTRACT,
  input  [1:0] VALID,
  output CARRY,
  output [15:0] RESULT,
  output RESULT_VALID
);

  wire BOTH_VALID_out;
  wire [15:0] adder_1_out, subtractor_1_out;

  Adder #(.width(16)) adder_1 (.a(OPERANDS[15:0]), .b(OPERANDS[31:16]), .out(adder_1_out), .cin(1'b1), .cout(CARRY));
  Subtractor #(.width(16)) subtractor_1 (
    .a(OPERANDS[15:0]), .b(OPERANDS[31:16]), .out(subtractor_1_out));  // open: bin, bout
  and BOTH_VALID (BOTH_VALID_out, VALID[0], VALID[1]);
  and ACTIVE_VALID (RESULT_VALID, SUBTRACT, BOTH_VALID_out);
  Multiplexer #(.width(16)) multiplexer_1 (.in0(adder_1_out), .in1(subtractor_1_out), .out(RESULT), .sel(SUBTRACT));

  // Notes on the sheet:
  //   ADD / SUB — gebündelte Operanden- und Validitätsbusse
endmodule

module Datapath (
  input  [15:0] DATA_IN,
  input  ACC_LOAD,
  input  VALID_IN,
  input  CLK,
  output [15:0] ACC_OUT,
  output ZERO,
  output NEGATIVE,
  output ACC_VALID_OUT
);

  Register #(.width(16)) ACC (.D(DATA_IN), .en(ACC_LOAD), .clk(CLK), .Q(ACC_OUT));  // open: clr
  Register #(.width(1)) ACC_VALID (.D(VALID_IN), .en(CLK), .clk(ACC_LOAD), .Q(ACC_VALID_OUT));  // open: clr
  Comparator #(.width(16)) comparator_1 (.a(ACC_OUT), .b({16{1'b0}}), .eq(ZERO), .lt(NEGATIVE));  // open: gt

  // Notes on the sheet:
  //   Clocked 16-bit accumulator; signed comparator derives ZERO and NEGATIVE
endmodule

module AddressPath (
  input  [15:0] ADDRESS_IN,
  input  AR_LOAD,
  input  [15:0] OFFSET,
  input  VALID_IN,
  input  CLK,
  output [15:0] ADDRESS,
  output [15:0] ADDRESS_PLUS_OFFSET,
  output OFFSET_CARRY,
  output ADDRESS_VALID
);

  Register #(.width(16)) AR (.D(ADDRESS_IN), .en(AR_LOAD), .clk(CLK), .Q(ADDRESS));  // open: clr
  Register #(.width(1)) AR_VALID (.D(VALID_IN), .en(AR_LOAD), .clk(CLK), .Q(ADDRESS_VALID));  // open: clr
  Adder #(.width(16)) adder_1 (.a(ADDRESS), .b(OFFSET), .out(ADDRESS_PLUS_OFFSET), .cout(OFFSET_CARRY));  // open: cin

  // Notes on the sheet:
  //   Clocked 12-bit address register with combinational offset addition
endmodule

module Memory (
  input  [15:0] ADDRESS,
  input  WRITE_ENABLE,
  input  CLK,
  input  VALID_IN,
  input  [15:0] DATA_IN,
  output VALID_OUT,
  output [15:0] DATA_OUT
);

  RAM #(.addrWidth(12), .dataWidth(1)) VALID_RAM (
    .addr(ADDRESS[11:0]), .we(WRITE_ENABLE), .oe(1'b1), .clk(CLK), .din(VALID_IN), .dout(VALID_OUT));
  RAM #(.addrWidth(12), .dataWidth(16)) DATA_RAM (
    .addr(ADDRESS[11:0]), .we(WRITE_ENABLE), .oe(1'b1), .clk(CLK), .din(DATA_IN), .dout(DATA_OUT));

  // Notes on the sheet:
  //   4096-word value/valid memory with shared address, write-enable, and clock
endmodule

module ErrorFlags (
  input  CLEAR_ERROR,
  input  CLK,
  input  SET_OVF,
  input  SET_DIV0,
  input  SET_ADDR,
  input  SET_INV,
  input  SET_ILL,
  input  SET_INPUT,
  output OVF_OUT,
  output DIV0_OUT,
  output ADDR_OUT,
  output INV_OUT,
  output ILL_OUT,
  output INPUT_OUT
);

  wire HOLD_ADDR_out, HOLD_DIV0_out, HOLD_ILL_out, HOLD_INPUT_out, HOLD_INV_out, HOLD_OVF_out, NEXT_ADDR_out,
       NEXT_DIV0_out, NEXT_ILL_out, NEXT_INPUT_out, NEXT_INV_out, NEXT_OVF_out, NOT_CLEAR_ERROR_out;

  not NOT_CLEAR_ERROR (NOT_CLEAR_ERROR_out, CLEAR_ERROR);
  and HOLD_OVF (HOLD_OVF_out, OVF_OUT, NOT_CLEAR_ERROR_out);
  and HOLD_DIV0 (HOLD_DIV0_out, DIV0_OUT, NOT_CLEAR_ERROR_out);
  and HOLD_ADDR (HOLD_ADDR_out, ADDR_OUT, NOT_CLEAR_ERROR_out);
  and HOLD_INV (HOLD_INV_out, INV_OUT, NOT_CLEAR_ERROR_out);
  and HOLD_ILL (HOLD_ILL_out, ILL_OUT, NOT_CLEAR_ERROR_out);
  and HOLD_INPUT (HOLD_INPUT_out, INPUT_OUT, NOT_CLEAR_ERROR_out);
  or NEXT_OVF (NEXT_OVF_out, SET_OVF, HOLD_OVF_out);
  or NEXT_DIV0 (NEXT_DIV0_out, SET_DIV0, HOLD_DIV0_out);
  or NEXT_ADDR (NEXT_ADDR_out, SET_ADDR, HOLD_ADDR_out);
  or NEXT_INV (NEXT_INV_out, SET_INV, HOLD_INV_out);
  or NEXT_ILL (NEXT_ILL_out, SET_ILL, HOLD_ILL_out);
  or NEXT_INPUT (NEXT_INPUT_out, SET_INPUT, HOLD_INPUT_out);
  Register #(.width(1)) OVF (.D(NEXT_OVF_out), .en(1'b1), .clk(CLK), .Q(OVF_OUT));  // open: clr
  Register #(.width(1)) DIV0 (.D(NEXT_DIV0_out), .en(1'b1), .clk(CLK), .Q(DIV0_OUT));  // open: clr
  Register #(.width(1)) ADDR (.D(NEXT_ADDR_out), .en(1'b1), .clk(CLK), .Q(ADDR_OUT));  // open: clr
  Register #(.width(1)) INV (.D(NEXT_INV_out), .en(1'b1), .clk(CLK), .Q(INV_OUT));  // open: clr
  Register #(.width(1)) ILL (.D(NEXT_ILL_out), .en(1'b1), .clk(CLK), .Q(ILL_OUT));  // open: clr
  Register #(.width(1)) INPUT (.D(NEXT_INPUT_out), .en(1'b1), .clk(CLK), .Q(INPUT_OUT));  // open: clr

  // Notes on the sheet:
  //   Set-dominant sticky flags: SET OR (current AND NOT CLEAR_ERROR)
endmodule

module FetchDecode (
  input  DEC_JUMP_NOT_ZERO,
  input  NOT_ZERO,
  input  CLK,
  input  RESET,
  input  DEC_HALT_ERROR,
  input  [15:0] PROGRAM_LIMIT,
  output JUMP_NOT_ZERO,
  output HALT_ERROR,
  output [11:0] PC_OUT,
  output [21:0] OPCODE
);

  wire comparator_1_gt;
  wire [15:0] adder_1_out;
  wire [15:12] PC_q;

  Register #(.width(16)) PC (.D(adder_1_out), .en(1'b1), .clk(CLK), .Q({PC_q, PC_OUT}), .clr(RESET));
  Comparator #(.width(16)) comparator_1 (.a(PROGRAM_LIMIT), .b({PC_q, PC_OUT}), .gt(comparator_1_gt));  // open: eq, lt
  Adder #(.width(16)) adder_1 (.a({PC_q, PC_OUT}), .b({16{1'b1}}), .out(adder_1_out));  // open: cin, cout
  ROM #(.addrWidth(12), .dataWidth(22)) INSTRUCTION_ROM (.addr(PC_OUT), .data(OPCODE));
  and JNZ_TAKEN (JUMP_NOT_ZERO, DEC_JUMP_NOT_ZERO, NOT_ZERO);
  or ERROR_HALT (HALT_ERROR, comparator_1_gt, DEC_HALT_ERROR);

  // Notes on the sheet:
  //   PROGRAM_LIMIT: initial=0xfff
  //   AP 7 machine format v1: stable six-bit opcode allocation and encoder-generated ROM
  //   contents of INSTRUCTION_ROM (hex, n*v repeats v):
  //   ffff 1c0065 3 1c0064 2a0000 50065 1c0064 240004 2c0000
endmodule

module FetchDecodeControls (
  input  [5:0] OPCODE,
  output LOAD_CONST,
  output LOAD_ADDRESS,
  output LOAD_ADDRESS_REGISTER,
  output LOAD_ADDRESS_REGISTER_PLUS_OFFSET,
  output ADD_CONST,
  output ADD_ADDRESS,
  output ADD_ADDRESS_REGISTER,
  output ADD_ADDRESS_REGISTER_PLUS_OFFSET,
  output SUB_CONST,
  output SUB_ADDRESS,
  output SUB_ADDRESS_REGISTER,
  output SUB_ADDRESS_REGISTER_PLUS_OFFSET,
  output MUL_CONST,
  output MUL_ADDRESS,
  output MUL_ADDRESS_REGISTER,
  output MUL_ADDRESS_REGISTER_PLUS_OFFSET,
  output DIV_CONST,
  output DIV_ADDRESS,
  output DIV_ADDRESS_REGISTER,
  output DIV_ADDRESS_REGISTER_PLUS_OFFSET,
  output AND_CONST,
  output AND_ADDRESS,
  output AND_ADDRESS_REGISTER,
  output AND_ADDRESS_REGISTER_PLUS_OFFSET,
  output OR_CONST,
  output OR_ADDRESS,
  output OR_ADDRESS_REGISTER,
  output OR_ADDRESS_REGISTER_PLUS_OFFSET,
  output STORE_ADDRESS,
  output STORE_ADDRESS_REGISTER,
  output STORE_ADDRESS_REGISTER_PLUS_OFFSET,
  output LOAD_ADDRESS_REGISTER_CONST,
  output LOAD_ADDRESS_REGISTER_ADDRESS,
  output NOT,
  output JUMP_ADDRESS,
  output JUMP_ZERO,
  output JUMP_NEGATIVE,
  output JUMP_ERROR,
  output JUMP_NOT_ERROR,
  output CLEAR_ERROR,
  output INPUT,
  output PRINT,
  output PRINT_ADDRESS,
  output HALT,
  output HALT_ERROR,
  output SET_OVF,
  output SET_DIV0,
  output SET_ADDR,
  output SET_INV,
  output SET_ILL,
  output SET_INPUT
);

  Decoder #(.select(6)) decoder_1 (
    .out0(LOAD_CONST), .out1(LOAD_ADDRESS), .out2(LOAD_ADDRESS_REGISTER),
    .out3(LOAD_ADDRESS_REGISTER_PLUS_OFFSET), .out4(ADD_CONST), .out5(ADD_ADDRESS),
    .out6(ADD_ADDRESS_REGISTER), .out7(ADD_ADDRESS_REGISTER_PLUS_OFFSET), .out8(SUB_CONST),
    .out9(SUB_ADDRESS), .out10(SUB_ADDRESS_REGISTER), .out11(SUB_ADDRESS_REGISTER_PLUS_OFFSET),
    .out12(MUL_CONST), .out13(MUL_ADDRESS), .out14(MUL_ADDRESS_REGISTER),
    .out15(MUL_ADDRESS_REGISTER_PLUS_OFFSET), .out16(DIV_CONST), .out17(DIV_ADDRESS),
    .out18(DIV_ADDRESS_REGISTER), .out19(DIV_ADDRESS_REGISTER_PLUS_OFFSET), .out20(AND_CONST),
    .out21(AND_ADDRESS), .out22(AND_ADDRESS_REGISTER), .out23(AND_ADDRESS_REGISTER_PLUS_OFFSET),
    .out24(OR_CONST), .out25(OR_ADDRESS), .out26(OR_ADDRESS_REGISTER),
    .out27(OR_ADDRESS_REGISTER_PLUS_OFFSET), .out28(STORE_ADDRESS), .out29(STORE_ADDRESS_REGISTER),
    .out30(STORE_ADDRESS_REGISTER_PLUS_OFFSET), .out31(LOAD_ADDRESS_REGISTER_CONST),
    .out32(LOAD_ADDRESS_REGISTER_ADDRESS), .out33(NOT), .out34(JUMP_ADDRESS), .out35(JUMP_ZERO),
    .out36(JUMP_NEGATIVE), .out37(JUMP_ERROR), .out38(JUMP_NOT_ERROR), .out39(CLEAR_ERROR), .out40(INPUT),
    .out41(PRINT), .out42(PRINT_ADDRESS), .out43(HALT), .out44(HALT_ERROR), .out45(SET_OVF),
    .out46(SET_DIV0), .out47(SET_ADDR), .out48(SET_INV), .out49(SET_ILL), .out50(SET_INPUT), .sel(OPCODE));  // open: out51, out52, out53, out54, out55, out56, out57, out58, out59, out60, out61, out62, out63, en
endmodule

module IntegrationClock (
  input  CLK,
  output FETCH_CLK,
  output DATAPATH_CLK,
  output ADDRESS_CLK,
  output MEMORY_CLK,
  output ERROR_FLAGS_CLK
);


  assign ADDRESS_CLK = CLK;
  assign DATAPATH_CLK = CLK;
  assign ERROR_FLAGS_CLK = CLK;
  assign FETCH_CLK = CLK;
  assign MEMORY_CLK = CLK;
endmodule

module IntegrationReset (
  input  RESET,
  output FETCH_RESET
);


  assign FETCH_RESET = RESET;
endmodule

module TinyCPU (
  input  CLK,
  input  RESET,
  input  [15:0] INPUT_VALUE,
  input  INPUT_VALID
);

  wire addsubcircuit_1_add_valid, datapath_1_acc_valid_out, decodesignals_1_acc_memory_requesst,
       decodesignals_1_accc_write_request, fetchdecodecontrols_1_add_address,
       fetchdecodecontrols_1_add_address_register, fetchdecodecontrols_1_add_address_register_plus_offset,
       fetchdecodecontrols_1_add_const, fetchdecodecontrols_1_clear_error, fetchdecodecontrols_1_input,
       fetchdecodecontrols_1_jump_zero, fetchdecodecontrols_1_not, fetchdecodecontrols_1_set_addr,
       fetchdecodecontrols_1_set_div0, fetchdecodecontrols_1_set_ill, fetchdecodecontrols_1_set_input,
       fetchdecodecontrols_1_set_inv, fetchdecodecontrols_1_set_ovf, fetchdecodecontrols_1_sub_address,
       fetchdecodecontrols_1_sub_address_register, fetchdecodecontrols_1_sub_address_register_plus_offset,
       fetchdecodecontrols_1_sub_const, memory_1_valid_out, multiplexer_6_out, multiplexer_7_out,
       subvalidcircuit_1_p5, subvalidcircuit_1_p8, undriven, undriven_2;
  wire [15:0] ACC_NOT_VALUE_out, datapath_1_acc_out, memory_1_data_out, multiplexer_1_out, multiplexer_2_out,
       multiplexer_3_out, multiplexer_4_out, multiplexer_5_out, subtractor_1_out;
  wire [21:0] fetchdecode_1_opcode;

  FetchDecode fetchdecode_1 (
    .RESET(RESET), .OPCODE(fetchdecode_1_opcode));  // open: DEC_JUMP_NOT_ZERO, NOT_ZERO, CLK, DEC_HALT_ERROR, PROGRAM_LIMIT, JUMP_NOT_ZERO, HALT_ERROR, PC_OUT
  Memory memory_1 (
    .CLK(CLK), .VALID_OUT(memory_1_valid_out), .DATA_OUT(memory_1_data_out));  // open: ADDRESS, WRITE_ENABLE, VALID_IN, DATA_IN
  DecodeSignals decodesignals_1 (
    .Opcode(fetchdecode_1_opcode[21:16]), .ACC_MEMORY_REQUESST(decodesignals_1_acc_memory_requesst),
    .ACCC_WRITE_REQUEST(decodesignals_1_accc_write_request));
  FetchDecodeControls fetchdecodecontrols_1 (
    .OPCODE(fetchdecode_1_opcode[21:16]), .ADD_CONST(fetchdecodecontrols_1_add_const),
    .ADD_ADDRESS(fetchdecodecontrols_1_add_address),
    .ADD_ADDRESS_REGISTER(fetchdecodecontrols_1_add_address_register),
    .ADD_ADDRESS_REGISTER_PLUS_OFFSET(fetchdecodecontrols_1_add_address_register_plus_offset),
    .SUB_CONST(fetchdecodecontrols_1_sub_const), .SUB_ADDRESS(fetchdecodecontrols_1_sub_address),
    .SUB_ADDRESS_REGISTER(fetchdecodecontrols_1_sub_address_register),
    .SUB_ADDRESS_REGISTER_PLUS_OFFSET(fetchdecodecontrols_1_sub_address_register_plus_offset),
    .NOT(fetchdecodecontrols_1_not), .JUMP_ZERO(fetchdecodecontrols_1_jump_zero),
    .CLEAR_ERROR(fetchdecodecontrols_1_clear_error), .INPUT(fetchdecodecontrols_1_input),
    .SET_OVF(fetchdecodecontrols_1_set_ovf), .SET_DIV0(fetchdecodecontrols_1_set_div0),
    .SET_ADDR(fetchdecodecontrols_1_set_addr), .SET_INV(fetchdecodecontrols_1_set_inv),
    .SET_ILL(fetchdecodecontrols_1_set_ill), .SET_INPUT(fetchdecodecontrols_1_set_input));  // open: LOAD_CONST, LOAD_ADDRESS, LOAD_ADDRESS_REGISTER, LOAD_ADDRESS_REGISTER_PLUS_OFFSET, MUL_CONST, MUL_ADDRESS, MUL_ADDRESS_REGISTER, MUL_ADDRESS_REGISTER_PLUS_OFFSET, DIV_CONST, DIV_ADDRESS, DIV_ADDRESS_REGISTER, DIV_ADDRESS_REGISTER_PLUS_OFFSET, AND_CONST, AND_ADDRESS, AND_ADDRESS_REGISTER, AND_ADDRESS_REGISTER_PLUS_OFFSET, OR_CONST, OR_ADDRESS, OR_ADDRESS_REGISTER, OR_ADDRESS_REGISTER_PLUS_OFFSET, STORE_ADDRESS, STORE_ADDRESS_REGISTER, STORE_ADDRESS_REGISTER_PLUS_OFFSET, LOAD_ADDRESS_REGISTER_CONST, LOAD_ADDRESS_REGISTER_ADDRESS, JUMP_ADDRESS, JUMP_NEGATIVE, JUMP_ERROR, JUMP_NOT_ERROR, PRINT, PRINT_ADDRESS, HALT, HALT_ERROR
  AddressPath addresspath_1 (.AR_LOAD(decodesignals_1_accc_write_request));  // open: ADDRESS_IN, OFFSET, VALID_IN, CLK, ADDRESS, ADDRESS_PLUS_OFFSET, OFFSET_CARRY, ADDRESS_VALID
  Datapath datapath_1 (
    .DATA_IN(multiplexer_5_out), .VALID_IN(multiplexer_7_out), .CLK(CLK), .ACC_OUT(datapath_1_acc_out),
    .ACC_VALID_OUT(datapath_1_acc_valid_out));  // open: ACC_LOAD, ZERO, NEGATIVE
  Multiplexer #(.width(16)) multiplexer_1 (
    .in0(fetchdecode_1_opcode[15:0]), .in1(memory_1_data_out), .out(multiplexer_1_out),
    .sel(decodesignals_1_acc_memory_requesst));
  assign ACC_NOT_VALUE_out = ~datapath_1_acc_out;  // NOT_Gate ACC_NOT_VALUE, 16 bits wide
  ErrorFlags errorflags_1 (
    .CLEAR_ERROR(fetchdecodecontrols_1_clear_error), .CLK(CLK), .SET_OVF(fetchdecodecontrols_1_set_ovf),
    .SET_DIV0(fetchdecodecontrols_1_set_div0), .SET_ADDR(fetchdecodecontrols_1_set_addr),
    .SET_INV(fetchdecodecontrols_1_set_inv), .SET_ILL(fetchdecodecontrols_1_set_ill),
    .SET_INPUT(fetchdecodecontrols_1_set_input));  // open: OVF_OUT, DIV0_OUT, ADDR_OUT, INV_OUT, ILL_OUT, INPUT_OUT
  Multiplexer #(.width(16)) multiplexer_2 (
    .in0(fetchdecode_1_opcode[15:0]), .in1(memory_1_data_out), .out(multiplexer_2_out), .sel(undriven));
  AddSubCircuit addsubcircuit_1 (
    .DEFAULT_VALID(memory_1_valid_out), .MEMORY_VALID(decodesignals_1_acc_memory_requesst),
    .ACC_VALID(datapath_1_acc_valid_out), .NOT_VALID_SELECT(fetchdecodecontrols_1_jump_zero),
    .ADD_ADDRESS(fetchdecodecontrols_1_add_address),
    .ADD_ADDRESS_REGISTER(fetchdecodecontrols_1_add_address_register),
    .ADD_ADDRESS_REGISTER_PLUS_OFFSET(fetchdecodecontrols_1_add_address_register_plus_offset),
    .ADD_CONST(fetchdecodecontrols_1_add_const), .ADD_VALID(addsubcircuit_1_add_valid));
  Multiplexer #(.width(16)) multiplexer_3 (
    .in0(multiplexer_1_out), .in1(ACC_NOT_VALUE_out), .out(multiplexer_3_out), .sel(fetchdecodecontrols_1_not));
  Subtractor #(.width(16)) subtractor_1 (
    .a(datapath_1_acc_out), .b(multiplexer_2_out), .out(subtractor_1_out));  // open: bin, bout
  Multiplexer #(.width(16)) multiplexer_4 (
    .in0(multiplexer_3_out), .in1(subtractor_1_out), .out(multiplexer_4_out));  // open: sel
  // SubValidCircuit subvalidcircuit_1: pin names not known; wires that end beside it: fetchdecodecontrols_1_sub_address_register_plus_offset, fetchdecodecontrols_1_sub_address_register, fetchdecodecontrols_1_sub_address, fetchdecodecontrols_1_sub_const, subvalidcircuit_1_p5, datapath_1_acc_valid_out, memory_1_valid_out, subvalidcircuit_1_p8
  Multiplexer #(.width(16)) multiplexer_5 (
    .in0(multiplexer_4_out), .in1(INPUT_VALUE), .out(multiplexer_5_out), .sel(fetchdecodecontrols_1_input));
  Multiplexer multiplexer_6 (
    .in0(addsubcircuit_1_add_valid), .in1(subvalidcircuit_1_p8), .out(multiplexer_6_out), .sel(undriven_2));
  Multiplexer multiplexer_7 (
    .in0(multiplexer_6_out), .in1(INPUT_VALID), .out(multiplexer_7_out), .sel(fetchdecodecontrols_1_input));

  // Notes on the sheet:
  //   MEMORY_DATA →
  //   ACC_VALUE →
  //   ACC_VALUE →
  //   MEMORY_RESULT →
  //   NOT_VALUE →
  //   NOT_VALUE →
  //   ACC_VALUE →
  //   SUB_ADDRESS/CONST →
  //   ALU_DATA →
  //   SUB_VALUE →
  //   SUB_VALUE →
  //   ALU_DATA →
  //   ALU_DATA →
  //   ALU_DATA →
  //   INPUT_VALUE →
  //   ALU_VALID →
  //   WRITE_DATA →
  //   ALU_VALID →
  //   SUB_VALID →
  //   ALU_VALID →
  //   ALU_VALID →
  //   INPUT_VALID →
  //   WRITE_VALID →
endmodule

module AddValidCircuit (
  input  ADD_ADDRESS,
  input  ADD_ADDRESS_REGISTER,
  input  ADD_ADDRESS_REGISTER_PLUS_OFFSET,
  input  ADD_CONST,
  input  MEMORY_VALID,
  input  ACC_VALID,
  output ADD_VALID
);

  wire ACC_ADD_FAMILY_SELECT_out, ACC_ADD_MEMORY_SELECT_out, multiplexer_1_out;

  buf ACC_ADD_MEMORY_SELECT (ACC_ADD_MEMORY_SELECT_out, ADD_ADDRESS_REGISTER);  // OR_Gate
  or ACC_ADD_FAMILY_SELECT (ACC_ADD_FAMILY_SELECT_out, ACC_ADD_MEMORY_SELECT_out, ADD_CONST);
  Multiplexer multiplexer_1 (.in0(1'b1), .in1(MEMORY_VALID), .out(multiplexer_1_out));  // open: sel
  and ACC_ADD_VALID (ADD_VALID, multiplexer_1_out, ACC_VALID);

  // Notes on the sheet:
  //   ADD_ADDRESS/CONST_VALID →
  //   ADD_OPERAND_VALID →
  //   ADD_VALID →
endmodule

module SubValidCircuit (
  input  SUB_ADDRESS,
  input  SUB_ADDRESS_REGISTER,
  input  SUB_ADDRESS_REGISTER_PLUS_OFFSET,
  input  SUB_CONST,
  input  MEMORY_VALID,
  input  ACC_VALID,
  output SUB_VALID
);

  wire ACC_SUB_FAMILY_SELECT_out, ACC_SUB_MEMORY_SELECT_out, multiplexer_1_out;

  buf ACC_SUB_MEMORY_SELECT (ACC_SUB_MEMORY_SELECT_out, SUB_ADDRESS_REGISTER);  // OR_Gate
  or ACC_SUB_FAMILY_SELECT (ACC_SUB_FAMILY_SELECT_out, ACC_SUB_MEMORY_SELECT_out, SUB_CONST);
  Multiplexer multiplexer_1 (.in0(1'b1), .in1(MEMORY_VALID), .out(multiplexer_1_out));  // open: sel
  and ACC_SUB_VALID (SUB_VALID, multiplexer_1_out, ACC_VALID);

  // Notes on the sheet:
  //   SUB_ADDRESS/CONST_VALID →
  //   SUB_OPERAND_VALID →
  //   SUB_VALID →
endmodule

module DecodeSignals (
  input  [5:0] Opcode,
  output ACC_MEMORY_REQUESST,
  output ACCC_WRITE_REQUEST
);

  wire ACC_LOAD_REQUEST_out, fetchdecodecontrols_1_add_address, fetchdecodecontrols_1_add_address_register,
       fetchdecodecontrols_1_add_address_register_plus_offset, fetchdecodecontrols_1_add_const,
       fetchdecodecontrols_1_and_address, fetchdecodecontrols_1_and_address_register,
       fetchdecodecontrols_1_and_address_register_plus_offset, fetchdecodecontrols_1_and_const,
       fetchdecodecontrols_1_div_address, fetchdecodecontrols_1_div_address_register,
       fetchdecodecontrols_1_div_address_register_plus_offset, fetchdecodecontrols_1_div_const,
       fetchdecodecontrols_1_input, fetchdecodecontrols_1_load_address,
       fetchdecodecontrols_1_load_address_register, fetchdecodecontrols_1_load_address_register_const,
       fetchdecodecontrols_1_load_address_register_plus_offset, fetchdecodecontrols_1_load_const,
       fetchdecodecontrols_1_mul_address, fetchdecodecontrols_1_mul_address_register,
       fetchdecodecontrols_1_mul_address_register_plus_offset, fetchdecodecontrols_1_mul_const,
       fetchdecodecontrols_1_not, fetchdecodecontrols_1_or_address,
       fetchdecodecontrols_1_or_address_register, fetchdecodecontrols_1_or_address_register_plus_offset,
       fetchdecodecontrols_1_or_const, fetchdecodecontrols_1_store_address,
       fetchdecodecontrols_1_store_address_register,
       fetchdecodecontrols_1_store_address_register_plus_offset, fetchdecodecontrols_1_sub_address,
       fetchdecodecontrols_1_sub_address_register, fetchdecodecontrols_1_sub_address_register_plus_offset,
       fetchdecodecontrols_1_sub_const;

  FetchDecodeControls fetchdecodecontrols_1 (
    .OPCODE(Opcode), .LOAD_CONST(fetchdecodecontrols_1_load_const),
    .LOAD_ADDRESS(fetchdecodecontrols_1_load_address),
    .LOAD_ADDRESS_REGISTER(fetchdecodecontrols_1_load_address_register),
    .LOAD_ADDRESS_REGISTER_PLUS_OFFSET(fetchdecodecontrols_1_load_address_register_plus_offset),
    .ADD_CONST(fetchdecodecontrols_1_add_const), .ADD_ADDRESS(fetchdecodecontrols_1_add_address),
    .ADD_ADDRESS_REGISTER(fetchdecodecontrols_1_add_address_register),
    .ADD_ADDRESS_REGISTER_PLUS_OFFSET(fetchdecodecontrols_1_add_address_register_plus_offset),
    .SUB_CONST(fetchdecodecontrols_1_sub_const), .SUB_ADDRESS(fetchdecodecontrols_1_sub_address),
    .SUB_ADDRESS_REGISTER(fetchdecodecontrols_1_sub_address_register),
    .SUB_ADDRESS_REGISTER_PLUS_OFFSET(fetchdecodecontrols_1_sub_address_register_plus_offset),
    .MUL_CONST(fetchdecodecontrols_1_mul_const), .MUL_ADDRESS(fetchdecodecontrols_1_mul_address),
    .MUL_ADDRESS_REGISTER(fetchdecodecontrols_1_mul_address_register),
    .MUL_ADDRESS_REGISTER_PLUS_OFFSET(fetchdecodecontrols_1_mul_address_register_plus_offset),
    .DIV_CONST(fetchdecodecontrols_1_div_const), .DIV_ADDRESS(fetchdecodecontrols_1_div_address),
    .DIV_ADDRESS_REGISTER(fetchdecodecontrols_1_div_address_register),
    .DIV_ADDRESS_REGISTER_PLUS_OFFSET(fetchdecodecontrols_1_div_address_register_plus_offset),
    .AND_CONST(fetchdecodecontrols_1_and_const), .AND_ADDRESS(fetchdecodecontrols_1_and_address),
    .AND_ADDRESS_REGISTER(fetchdecodecontrols_1_and_address_register),
    .AND_ADDRESS_REGISTER_PLUS_OFFSET(fetchdecodecontrols_1_and_address_register_plus_offset),
    .OR_CONST(fetchdecodecontrols_1_or_const), .OR_ADDRESS(fetchdecodecontrols_1_or_address),
    .OR_ADDRESS_REGISTER(fetchdecodecontrols_1_or_address_register),
    .OR_ADDRESS_REGISTER_PLUS_OFFSET(fetchdecodecontrols_1_or_address_register_plus_offset),
    .STORE_ADDRESS(fetchdecodecontrols_1_store_address),
    .STORE_ADDRESS_REGISTER(fetchdecodecontrols_1_store_address_register),
    .STORE_ADDRESS_REGISTER_PLUS_OFFSET(fetchdecodecontrols_1_store_address_register_plus_offset),
    .LOAD_ADDRESS_REGISTER_CONST(fetchdecodecontrols_1_load_address_register_const),
    .NOT(fetchdecodecontrols_1_not), .INPUT(fetchdecodecontrols_1_input));  // open: LOAD_ADDRESS_REGISTER_ADDRESS, JUMP_ADDRESS, JUMP_ZERO, JUMP_NEGATIVE, JUMP_ERROR, JUMP_NOT_ERROR, CLEAR_ERROR, PRINT, PRINT_ADDRESS, HALT, HALT_ERROR, SET_OVF, SET_DIV0, SET_ADDR, SET_INV, SET_ILL, SET_INPUT
  or ACC_LOAD_REQUEST (ACC_LOAD_REQUEST_out, fetchdecodecontrols_1_load_const, fetchdecodecontrols_1_load_address, fetchdecodecontrols_1_load_address_register, fetchdecodecontrols_1_load_address_register_plus_offset, fetchdecodecontrols_1_add_const, fetchdecodecontrols_1_add_address, fetchdecodecontrols_1_add_address_register, fetchdecodecontrols_1_add_address_register_plus_offset, fetchdecodecontrols_1_sub_const, fetchdecodecontrols_1_sub_address, fetchdecodecontrols_1_sub_address_register, fetchdecodecontrols_1_sub_address_register_plus_offset, fetchdecodecontrols_1_mul_const, fetchdecodecontrols_1_mul_address, fetchdecodecontrols_1_mul_address_register, fetchdecodecontrols_1_mul_address_register_plus_offset, fetchdecodecontrols_1_div_const, fetchdecodecontrols_1_div_address, fetchdecodecontrols_1_div_address_register, fetchdecodecontrols_1_div_address_register_plus_offset, fetchdecodecontrols_1_and_const, fetchdecodecontrols_1_and_address, fetchdecodecontrols_1_and_address_register, fetchdecodecontrols_1_and_address_register_plus_offset, fetchdecodecontrols_1_or_const, fetchdecodecontrols_1_or_address, fetchdecodecontrols_1_or_address_register, fetchdecodecontrols_1_or_address_register_plus_offset, fetchdecodecontrols_1_store_address, fetchdecodecontrols_1_store_address_register, fetchdecodecontrols_1_store_address_register_plus_offset, fetchdecodecontrols_1_load_address_register_const);
  or ACC_MEMORY_SELECT (ACC_MEMORY_REQUESST, fetchdecodecontrols_1_load_address, fetchdecodecontrols_1_load_address_register, fetchdecodecontrols_1_load_address_register_plus_offset);
  or ACC_WRITE_REQUEST (ACCC_WRITE_REQUEST, ACC_LOAD_REQUEST_out, fetchdecodecontrols_1_not, fetchdecodecontrols_1_input);
endmodule

module AddSubCircuit (
  input  DEFAULT_VALID,
  input  MEMORY_VALID,
  input  ACC_VALID,
  input  NOT_VALID_SELECT,
  input  ADD_ADDRESS,
  input  ADD_ADDRESS_REGISTER,
  input  ADD_ADDRESS_REGISTER_PLUS_OFFSET,
  input  ADD_CONST,
  output ADD_VALID
);

  wire ACC_ADD_MEMORY_SELECT_out, ACC_ADD_SELECT_out, ACC_ADD_VALID_out, multiplexer_1_out,
       multiplexer_2_out, multiplexer_3_out;

  or ACC_ADD_MEMORY_SELECT (ACC_ADD_MEMORY_SELECT_out, ADD_ADDRESS, ADD_ADDRESS_REGISTER, ADD_ADDRESS_REGISTER_PLUS_OFFSET);
  or ACC_ADD_SELECT (ACC_ADD_SELECT_out, ACC_ADD_MEMORY_SELECT_out, ADD_CONST);
  Multiplexer multiplexer_1 (.in0(1'b1), .in1(DEFAULT_VALID), .out(multiplexer_1_out), .sel(ACC_ADD_MEMORY_SELECT_out));
  buf ACC_ADD_VALID (ACC_ADD_VALID_out, ACC_VALID);  // AND_Gate
  Multiplexer multiplexer_2 (.in0(1'b1), .in1(DEFAULT_VALID), .out(multiplexer_2_out), .sel(MEMORY_VALID));
  Multiplexer multiplexer_3 (.in0(multiplexer_2_out), .in1(ACC_VALID), .out(multiplexer_3_out), .sel(NOT_VALID_SELECT));
  Multiplexer multiplexer_4 (
    .in0(multiplexer_3_out), .in1(ACC_ADD_VALID_out), .out(ADD_VALID), .sel(ACC_ADD_SELECT_out));

  // Notes on the sheet:
  //   ADD_ADDRESS/CONST_VALID →
  //   CONST_VALID →
  //   ADD_SELECT →
  //   ADD_OPERAND_VALID →
  //   MEMORY_VALID →
  //   ADD_VALID →
  //   DEFAULT_VALID →
  //   ADD_VALID →
  //   MEMORY_VALID →
  //   NOT_SELECT →
  //   ALU_VALID →
  //   ALU_VALID →
  //   ALU_VALID →
endmodule
