// Logisim project TinyCPU-AddSub.circ as structural Verilog: 1 circuit, main circuit AddSub
module AddSub (
  input  [31:0] OPERANDS,
  input  [1:0] VALID,
  input  SUBTRACT,
  output CARRY,
  output [15:0] RESULT,
  output RESULT_VALID
);

  wire BOTH_VALID_out;
  wire [15:0] adder_1_out, subtractor_1_out;

  Adder #(.width(16)) adder_1 (.a(OPERANDS[15:0]), .b(OPERANDS[31:16]), .out(adder_1_out), .cin(1'b1), .cout(CARRY));
  Subtractor #(.width(16)) subtractor_1 (
    .a(OPERANDS[15:0]), .b(OPERANDS[31:16]), .out(subtractor_1_out));  // open: bin, bout
  and BOTH_VALID (BOTH_VALID_out, VALID[0], VALID[1]);
  and ACTIVE_VALID (RESULT_VALID, BOTH_VALID_out, SUBTRACT);
  Multiplexer #(.width(16)) multiplexer_1 (.in0(adder_1_out), .in1(subtractor_1_out), .out(RESULT), .sel(SUBTRACT));

  // Notes on the sheet:
  //   ADD / SUB — gebündelte Operanden- und Validitätsbusse
endmodule
