// Logisim project TinyCPU-FetchDecode1.circ as structural Verilog: 1 circuit, main circuit FetchDecode
module FetchDecode (
  input  CLK,
  input  RESET,
  input  ZERO,
  input  [11:0] PROGRAM_LIMIT,
  input  NEGATIVE,
  input  ERROR
);

  Register #(.width(12)) PC ();  // open: D, en, clk, Q, clr
  Adder #(.width(12)) adder_1 ();  // open: a, b, out, cin, cout
  Multiplexer #(.width(12)) multiplexer_1 ();  // open: in0, in1, out, sel
  ROM #(.addrWidth(12), .dataWidth(22)) INSTRUCTION_ROM ();  // open: addr, data
  Comparator #(.width(12)) comparator_1 ();  // open: a, b, gt, eq, lt

  // Notes on the sheet:
  //   AP 7 machine format v1: stable six-bit opcode allocation and encoder-generated ROM
  //   contents of INSTRUCTION_ROM (hex, n*v repeats v):
  //   ffff 1c0065 3 1c0064 2a0000 50065 1c0064 240004 2c0000
endmodule
