// Logisim project TinyCPU-FetchDecode2.circ as structural Verilog: 1 circuit, main circuit FetchDecode
module FetchDecode (
  output [15:0] OPERAND,
  output LOAD_CONST,
  output STORE_ADDRESS,
  output ADD_ADDRESS,
  output JUMP_NOT_ZERO,
  output PRINT,
  output HALT,
  output SET_ADDR,
  output HALT_ERROR,
  output [11:0] PC_OUT
);

  // AND_Gate JNZ_TAKEN is placed but not wired
  // OR_Gate ERROR_HALT is placed but not wired

  // Notes on the sheet:
  //   AP 7 machine format v1: stable six-bit opcode allocation and encoder-generated ROM
endmodule
