// Logisim project TinyCPU-SubArithmeticCircuit.circ as structural Verilog: 1 circuit, main circuit SubArithmeticCircuit
module SubArithmeticCircuit (
  input  [15:0] LEFT,
  input  [15:0] RIGHT,
  input  INPUT_VALID,
  output [15:0] RESULT,
  output OVERFLOW,
  output RESULT_VALID
);

  wire NO_OVERFLOW_out, OPERAND_SIGN_DIFFERENT_out, RESULT_SIGN_CHANGED_out;

  Subtractor #(.width(16)) SUBTRACTOR (.a(LEFT), .b(RIGHT), .out(RESULT));  // open: bin, bout
  // XOR_Gate OPERAND_SIGN_DIFFERENT has open pins: out=OPERAND_SIGN_DIFFERENT_out
  // XOR_Gate RESULT_SIGN_CHANGED has open pins: out=RESULT_SIGN_CHANGED_out
  and SIGN_OVERFLOW (OVERFLOW, OPERAND_SIGN_DIFFERENT_out, RESULT_SIGN_CHANGED_out);
  not NO_OVERFLOW (NO_OVERFLOW_out, OVERFLOW);
  and RANGE_VALID (RESULT_VALID, NO_OVERFLOW_out, INPUT_VALID);

  // Notes on the sheet:
  //   signed SUB: overflow = (left_sign XOR right_sign) AND (left_sign XOR result_sign)
endmodule
