// Logisim project TinyCPU-SubValidCircuit.circ as structural Verilog: 1 circuit, main circuit SubValidCircuit
module SubValidCircuit (
  input  SUB_ADDRESS,
  input  SUB_ADDRESS_REGISTER,
  input  SUB_ADDRESS_REGISTER_PLUS_OFFSET,
  input  SUB_CONST,
  input  MEMORY_VALID,
  input  ACC_VALID,
  output SUB_VALID
);

  wire ACC_SUB_FAMILY_SELECT_out, ACC_SUB_MEMORY_SELECT_out, multiplexer_1_out;

  buf ACC_SUB_MEMORY_SELECT (ACC_SUB_MEMORY_SELECT_out, SUB_ADDRESS_REGISTER);  // OR_Gate
  or ACC_SUB_FAMILY_SELECT (ACC_SUB_FAMILY_SELECT_out, ACC_SUB_MEMORY_SELECT_out, SUB_CONST);
  Multiplexer multiplexer_1 (.in0(1'b1), .in1(MEMORY_VALID), .out(multiplexer_1_out));  // open: sel
  and ACC_SUB_VALID (SUB_VALID, multiplexer_1_out, ACC_VALID);

  // Notes on the sheet:
  //   SUB_ADDRESS/CONST_VALID →
  //   SUB_OPERAND_VALID →
  //   SUB_VALID →
endmodule
